// Logisim project 02fulsum.circ as structural Verilog
module hs (
  input  in_1,
  input  in_2,
  output out_3,
  output \nor 
);

  and and_1 (out_3, in_1, in_2);
  xor xor_1 (\nor , in_1, in_2);

  // Notes on the sheet:
  //   and
endmodule

module fs (
  input  in_1,
  input  in_2,
  input  in_3,
  output out_4,
  output out_5
);

  wire hs_1_nor, hs_1_out_3, hs_2_out_3;

  hs hs_1 (.in_1(in_1), .in_2(in_2), .out_3(hs_1_out_3), .\nor (hs_1_nor));
  or or_1 (out_4, hs_1_out_3, hs_2_out_3);
  hs hs_2 (.in_1(hs_1_nor), .in_2(in_3), .out_3(hs_2_out_3), .\nor (out_5));

  // Notes on the sheet:
  //   or
endmodule

module fbitsum (
  input  in_1,
  input  in_2,
  input  in_3,
  input  in_4,
  input  in_5,
  input  in_6,
  input  in_7,
  input  in_8
);

  wire fs_1_out_5, fs_2_out_4, fs_2_out_5, fs_3_out_4, fs_3_out_5, fs_4_out_4, fs_4_out_5;

  fs fs_1 (.in_1(in_1), .in_2(in_5), .in_3(fs_2_out_4), .out_5(fs_1_out_5));  // open: out_4
  fs fs_2 (.in_1(in_2), .in_2(in_6), .in_3(fs_3_out_4), .out_4(fs_2_out_4), .out_5(fs_2_out_5));
  fs fs_3 (.in_1(in_3), .in_2(in_7), .in_3(fs_4_out_4), .out_4(fs_3_out_4), .out_5(fs_3_out_5));
  fs fs_4 (.in_1(in_4), .in_2(in_8), .out_4(fs_4_out_4), .out_5(fs_4_out_5));  // open: in_3
  LED led_1 (.in(fs_1_out_5));
  LED led_2 (.in(fs_2_out_5));
  LED led_3 (.in(fs_3_out_5));
  LED led_4 (.in(fs_4_out_5));
endmodule

module mltiplexor (
  input  in_1,
  input  in_2,
  input  in_3,
  output out_4
);

  wire and_1_out, and_2_out, not_1_out;

  not not_1 (not_1_out, in_3);
  and and_1 (and_1_out, in_1, not_1_out);
  and and_2 (and_2_out, in_2, in_3);
  or or_1 (out_4, and_1_out, and_2_out);

  // Notes on the sheet:
  //   and
  //   and
  //   or
endmodule

module calcul (
  input  [7:0] in_1,
  input  [7:0] in_2,
  input  in_3,
  output [7:0] out_4
);

  wire [7:0] adder_1_out, multiplier_1_out;

  Adder adder_1 (.a(in_1), .b(in_2), .out(adder_1_out));  // open: cin, cout
  Multiplier multiplier_1 (.a(in_1), .b(in_2), .out(multiplier_1_out));  // open: cin, cout
  Multiplexer #(.width(8)) multiplexer_1 (.in0(adder_1_out), .in1(multiplier_1_out), .out(out_4), .sel(in_3));
endmodule

module srlatch (
  input  in_1,
  input  \nor ,
  output out_3
);

  wire nor_2_out;

  nor nor_1 (out_3, in_1, nor_2_out);
  nor nor_2 (nor_2_out, out_3, \nor );

  // Notes on the sheet:
  //   nor
endmodule

module dlatch (
  input  DATA,
  input  in_2,
  output out_3
);

  wire and_1_out, and_2_out, not_1_out, not_2_out;

  not not_1 (not_1_out, DATA);
  not not_2 (not_2_out, not_1_out);
  and and_1 (and_1_out, not_1_out, in_2);
  and and_2 (and_2_out, in_2, not_2_out);
  srlatch srlatch_1 (.in_1(and_1_out), .\nor (and_2_out), .out_3(out_3));

  // Notes on the sheet:
  //   STORE
  //   and
  //   and
endmodule

module regstr (
  input  [3:0] in_1,
  input  in_2,
  output [3:0] out_3
);

  dlatch dlatch_1 (.DATA(in_1[3]), .in_2(in_2), .out_3(out_3[3]));
  dlatch dlatch_2 (.DATA(in_1[2]), .in_2(in_2), .out_3(out_3[2]));
  dlatch dlatch_3 (.DATA(in_1[1]), .in_2(in_2), .out_3(out_3[1]));
  dlatch dlatch_4 (.DATA(in_1[0]), .in_2(in_2), .out_3(out_3[0]));
endmodule

module myram (
  input  [3:0] in_1,
  input  in_2,
  input  [1:0] ADDRESS,
  output [3:0] out_4
);

  wire and_1_out, and_2_out, and_3_out, and_4_out, deshifr_1_and, deshifr_1_and_2, deshifr_1_and_3,
       deshifr_1_and_4;
  wire [3:0] regstr_1_out_3, regstr_2_out_3, regstr_3_out_3, regstr_4_out_3;

  deshifr deshifr_1 (
    .in_1(ADDRESS), .\and (deshifr_1_and), .and_2(deshifr_1_and_2), .and_3(deshifr_1_and_3),
    .and_4(deshifr_1_and_4));
  and and_1 (and_1_out, in_2, deshifr_1_and);
  and and_2 (and_2_out, in_2, deshifr_1_and_2);
  and and_3 (and_3_out, in_2, deshifr_1_and_3);
  and and_4 (and_4_out, in_2, deshifr_1_and_4);
  regstr regstr_1 (.in_1(in_1), .in_2(and_1_out), .out_3(regstr_1_out_3));
  regstr regstr_2 (.in_1(in_1), .in_2(and_2_out), .out_3(regstr_2_out_3));
  regstr regstr_3 (.in_1(in_1), .in_2(and_3_out), .out_3(regstr_3_out_3));
  regstr regstr_4 (.in_1(in_1), .in_2(and_4_out), .out_3(regstr_4_out_3));
  Multiplexer #(.select(2), .width(4)) multiplexer_1 (
    .in0(regstr_1_out_3), .in1(regstr_2_out_3), .in2(regstr_3_out_3), .in3(regstr_4_out_3), .out(out_4),
    .sel(ADDRESS));

  // Notes on the sheet:
  //   DATA IN
  //   WRITE
  //   and
  //   and
  //   and
  //   and
endmodule

module deshifr (
  input  [1:0] in_1,
  output \and ,
  output and_2,
  output and_3,
  output and_4
);

  wire not_1_out, not_2_out, not_3_out, not_4_out;

  not not_1 (not_1_out, in_1[0]);
  not not_2 (not_2_out, in_1[1]);
  not not_3 (not_3_out, in_1[1]);
  not not_4 (not_4_out, in_1[0]);
  and and_1 (\and , not_1_out, not_2_out);
  and u_and_2 (and_2, in_1[0], not_3_out);
  and u_and_3 (and_3, not_4_out, in_1[1]);
  and u_and_4 (and_4, in_1[0], in_1[1]);
endmodule

module pcalc (
);

  wire [7:0] calcul_1_out_4, register_1_q, register_2_q;

  Register register_1 (.Q(register_1_q));  // open: D, en, clk, clr
  Register register_2 (.Q(register_2_q));  // open: D, en, clk, clr
  calcul calcul_1 (.in_1(register_1_q), .in_2(register_2_q), .out_4(calcul_1_out_4));  // open: in_3
  Register register_3 (.D(calcul_1_out_4));  // open: en, clk, Q, clr
endmodule
